# Fritzing sketch RPi_RC5221 (saved by Fritzing 0.9.5d)
breadboards: 1

parts:
  Mod1 = Raspberry Pi 4B
  元件1 = RFID-RC522-v3

nets:
  3V3: Mod1.3V3, 元件1.3.3V
  GND: Mod1.GND, 元件1.GND
  N1: Mod1.GPIO10, 元件1.MOSI
  N2: Mod1.GPIO9, 元件1.MISO
  N3: Mod1.GPIO25, 元件1.RST
  N4: Mod1.GPIO11, 元件1.SCK
  N5: Mod1.GPIO8, 元件1.SDA

notes:
  Gacha接腳圖

custom parts:
  RFID-RC522-v3: A simple China made RFID-RC522 Reader (6x4 cm); do check the pin labels, as this is a MFRC522 based clone.
